// Logisim project OneAddress.circ as structural Verilog: 7 circuits, main circuit CPU-Main
module ALU (
  input  [15:0] AC,
  input  [15:0] Y,
  input  [3:0] ALUOp,
  output [15:0] Output,
  output Overflow
);

  wire adder_1_cout, adder_2_cout, xor_16_out;
  wire [14:0] xor_1_out;

  xor xor_1 (xor_1_out[0], Y[0], ALUOp[0]);
  xor xor_2 (xor_1_out[2], Y[2], ALUOp[0]);
  xor xor_3 (xor_1_out[4], Y[4], ALUOp[0]);
  xor xor_4 (xor_1_out[6], Y[6], ALUOp[0]);
  xor xor_5 (xor_1_out[8], Y[8], ALUOp[0]);
  xor xor_6 (xor_1_out[10], Y[10], ALUOp[0]);
  xor xor_7 (xor_1_out[12], Y[12], ALUOp[0]);
  xor xor_8 (xor_1_out[14], Y[14], ALUOp[0]);
  xor xor_9 (xor_1_out[1], Y[1], ALUOp[0]);
  xor xor_10 (xor_1_out[3], Y[3], ALUOp[0]);
  xor xor_11 (xor_1_out[5], Y[5], ALUOp[0]);
  xor xor_12 (xor_1_out[7], Y[7], ALUOp[0]);
  xor xor_13 (xor_1_out[9], Y[9], ALUOp[0]);
  xor xor_14 (xor_1_out[11], Y[11], ALUOp[0]);
  xor xor_15 (xor_1_out[13], Y[13], ALUOp[0]);
  xor xor_16 (xor_16_out, Y[15], ALUOp[0]);
  Adder #(.width(15)) adder_1 (.a(AC[14:0]), .b(xor_1_out), .out(Output[14:0]), .cin(ALUOp[0]), .cout(adder_1_cout));
  Adder #(.width(1)) adder_2 (.a(AC[15]), .b(xor_16_out), .out(Output[15]), .cin(adder_1_cout), .cout(adder_2_cout));
  xor xor_17 (Overflow, adder_1_cout, adder_2_cout);

  // Notes on the sheet:
  //   0000 = add
  //   0001 = sub
endmodule

module Control_Unit (
  input  [7:0] Instruction,
  output [3:0] ALUOp,
  output WriteAc,
  output ALUSrc,
  output ClrAC,
  output MemWr,
  output Branch,
  output BR
);

  wire decoder_1_out2;

  Decoder #(.select(4), .enable("false")) decoder_1 (
    .out1(ALUSrc), .out2(decoder_1_out2), .out3(ClrAC), .out4(MemWr), .out5(Branch), .out6(BR),
    .sel(Instruction[7:4]));  // open: out0, out7, out8, out9, out10, out11, out12, out13, out14, out15
  or or_1 (WriteAc, ALUSrc, decoder_1_out2, ClrAC);

  assign ALUOp = Instruction[3:0];
endmodule

module SignExtend (
  input  [7:0] Immediate,
  output [15:0] SignExtValue
);


  assign SignExtValue = {{9{Immediate[7]}}, Immediate[6:0]};
endmodule

module CPU_Main (
);

  wire and_1_out, button_1_out, clock_1_out, comparator_1_eq, control_unit_1_alusrc, control_unit_1_br,
       control_unit_1_branch, control_unit_1_clrac, control_unit_1_memwr, control_unit_1_writeac, or_1_out;
  wire [3:0] control_unit_1_aluop;
  wire [7:0] adder_1_out, multiplexer_1_out, PC_q, ram_1_data;
  wire [15:0] AC_q, alu1_1_output, multiplexer_2_out, multiplexer_3_out, ram_2_data,
       signextend_1_signextvalue;
  wire [15:8] ram_1_data_2;

  Clock clock_1 (.out(clock_1_out));
  Button button_1 (.out(button_1_out));
  Adder adder_1 (.a(PC_q), .b(8'h1), .out(adder_1_out));  // open: cin, cout
  or or_1 (or_1_out, and_1_out, control_unit_1_br);
  and and_1 (and_1_out, comparator_1_eq, control_unit_1_branch);
  Multiplexer #(.width(8), .enable("false")) multiplexer_1 (
    .in0(adder_1_out), .in1(ram_1_data), .out(multiplexer_1_out), .sel(or_1_out));
  Register PC (.D(multiplexer_1_out), .en(1'b1), .Q(PC_q), .clk(clock_1_out), .clr(button_1_out));
  RAM #(.dataWidth(16)) ram_1 (
    .addr(PC_q), .data({ram_1_data_2, ram_1_data}), .clk(clock_1_out));  // open: sel, ld, clr
  Control_Unit control_unit_1 (
    .Instruction(ram_1_data_2), .ALUOp(control_unit_1_aluop), .WriteAc(control_unit_1_writeac),
    .ALUSrc(control_unit_1_alusrc), .ClrAC(control_unit_1_clrac), .MemWr(control_unit_1_memwr),
    .Branch(control_unit_1_branch), .BR(control_unit_1_br));
  RAM #(.dataWidth(16), .bus("separate")) ram_2 (
    .addr(ram_1_data), .din(AC_q), .data(ram_2_data), .str(control_unit_1_memwr), .sel(1'b1),
    .clk(clock_1_out), .ld(1'b1));  // open: clr
  SignExtend signextend_1 (.Immediate(ram_1_data), .SignExtValue(signextend_1_signextvalue));
  Multiplexer #(.width(16), .enable("false")) multiplexer_2 (
    .in0(alu1_1_output), .in1({16{1'b0}}), .out(multiplexer_2_out), .sel(control_unit_1_clrac));
  Register #(.width(16)) AC (
    .D(multiplexer_2_out), .en(control_unit_1_writeac), .Q(AC_q), .clk(clock_1_out), .clr(button_1_out));
  Multiplexer #(.width(16), .enable("false")) multiplexer_3 (
    .in0(ram_2_data), .in1(signextend_1_signextvalue), .out(multiplexer_3_out), .sel(control_unit_1_alusrc));
  Comparator #(.width(16)) comparator_1 (.a(AC_q), .b({16{1'b0}}), .eq(comparator_1_eq));  // open: gt, lt
  ALU1 alu1_1 (.AC(AC_q), .Y(multiplexer_3_out), .ALUOp(control_unit_1_aluop), .Output(alu1_1_output));

  // Notes on the sheet:
  //   Reset PC
  //   Increment PC
  //   Branch Address
  //   Next Instr
  //   Select Branch if Branc = true and ALU is zero
  //   Text (Program) Memory
  //   Control Unit
  //   Data Memory
  //   Sign Extend
  //   Mem Data
  //   Immediate
  //   AC tp Memory
  //   Select ALU Input
  //   AC to ALU
  //   ALU to AC
  //   ALU
  //   ALUOpt
endmodule

module CPU_Arithmetic_Subsection (
);

  wire undriven, undriven_2, undriven_3, undriven_4, undriven_5;
  wire [3:0] undriven_6;
  wire [15:0] AC_q, alu_1_output, multiplexer_1_out, multiplexer_2_out, ram_1_data, signextend_1_signextvalue;

  RAM #(.dataWidth(16), .bus("separate")) ram_1 (
    .addr({8{1'b0}}), .din(AC_q), .data(ram_1_data), .str(undriven), .sel(1'b1), .clk(undriven_2), .ld(1'b1));  // open: clr
  SignExtend signextend_1 (.Immediate({8{1'b0}}), .SignExtValue(signextend_1_signextvalue));
  Multiplexer #(.width(16), .enable("false")) multiplexer_1 (
    .in0(alu_1_output), .in1({16{1'b0}}), .out(multiplexer_1_out), .sel(undriven_3));
  Register #(.width(16)) AC (.D(multiplexer_1_out), .en(undriven_4), .Q(AC_q), .clk(undriven_2));  // open: clr
  Multiplexer #(.width(16), .enable("false")) multiplexer_2 (
    .in0(ram_1_data), .in1(signextend_1_signextvalue), .out(multiplexer_2_out), .sel(undriven_5));
  ALU alu_1 (.AC(AC_q), .Y(multiplexer_2_out), .ALUOp(undriven_6), .Output(alu_1_output));  // open: Overflow

  // Notes on the sheet:
  //   Control Wires
  //   Data Memory
  //   MemWr
  //   Clock
  //   Sign Extend
  //   WriteAC
  //   ClrAC
  //   Mem Data
  //   Immediate
  //   Select ALU Input
  //   ALUSrc
  //   AC to ALU
  //   ALUOpt
  //   ALU to AC
  //   ALU
endmodule

module CPU___Execution_Control (
);

  wire and_1_out, clock_1_out, comparator_1_eq, control_unit_1_p2, control_unit_1_p3, control_unit_1_p4,
       control_unit_1_p5, control_unit_1_p6, control_unit_1_p7;
  wire [7:0] adder_1_out, multiplexer_1_out, PC_q, ram_1_data;
  wire [15:0] undriven;
  wire [15:8] ram_1_data_2;

  Clock clock_1 (.out(clock_1_out));
  Adder adder_1 (.a(PC_q), .b(8'h1), .out(adder_1_out));  // open: cin, cout
  and and_1 (and_1_out, comparator_1_eq, control_unit_1_p7);
  Multiplexer #(.width(8), .enable("false")) multiplexer_1 (
    .in0(adder_1_out), .in1(ram_1_data), .out(multiplexer_1_out), .sel(and_1_out));
  Register PC (.D(multiplexer_1_out), .en(1'b1), .Q(PC_q), .clk(clock_1_out));  // open: clr
  RAM #(.dataWidth(16)) ram_1 (
    .addr(PC_q), .data({ram_1_data_2, ram_1_data}), .clk(clock_1_out));  // open: sel, ld, clr
  // Control_Unit control_unit_1: pin names not known; wires that end beside it: ram_1_data_2, control_unit_1_p2, control_unit_1_p3, control_unit_1_p4, control_unit_1_p5, control_unit_1_p6, control_unit_1_p7
  Comparator #(.width(16)) comparator_1 (.a(undriven), .b({16{1'b0}}), .eq(comparator_1_eq));  // open: gt, lt

  // Notes on the sheet:
  //   Reset PC
  //   Increment PC
  //   Branch Address
  //   Next Instr
  //   Select Branch if Branc = true and ALU is zero
  //   Text (Program) Memory
  //   Immediate Value to DM
  //   Immediate Value to ALU
  //   Control Unit
  //   Beqz
  //   Value From ALU
  //   Comparator
endmodule

module ALU1 (
  input  [15:0] AC,
  input  [15:0] Y,
  input  [3:0] ALUOp,
  output [15:0] Output
);

  wire [15:0] adder_1_out, and_1_out, divider_1_out, divider_1_rem, multiplier_1_out, shifter_1_out,
       subtractor_1_out;

  Adder #(.width(16)) adder_1 (.a(AC), .b(Y), .out(adder_1_out));  // open: cin, cout
  Subtractor #(.width(16)) subtractor_1 (.a(AC), .b(Y), .out(subtractor_1_out));  // open: bin, bout
  Multiplier #(.width(16)) multiplier_1 (.a(AC), .b(Y), .out(multiplier_1_out));  // open: cin, cout
  Divider #(.width(16)) divider_1 (.a(AC), .b(Y), .out(divider_1_out), .rem(divider_1_rem));  // open: upper
  assign and_1_out = AC & Y;  // AND_Gate and_1, 16 bits wide
  Shifter #(.width(16)) shifter_1 (.in(AC), .\dist (Y[3:0]), .out(shifter_1_out));
  Multiplexer #(.select(4), .width(16), .enable("false")) multiplexer_1 (
    .in0(adder_1_out), .in1(subtractor_1_out), .in2(multiplier_1_out), .in3(divider_1_out),
    .in4(divider_1_rem), .in5(and_1_out), .in6(shifter_1_out), .out(Output), .sel(ALUOp));  // open: in7, in8, in9, in10, in11, in12, in13, in14, in15

  // Notes on the sheet:
  //   0000 = add
  //   0001 = sub
  //   0010 = mul
  //   0011 = div
  //   0100 = rem
  //   0101 = and
  //   0110 = shift
endmodule
